# Fritzing sketch HondenvoederFritzing (saved by Fritzing 0.9.3b)
breadboards: 2

parts:
  Part1 = Arduino Uno (Rev3)  # not connected
  Part2 = Arduino Ethernet Shield (Rev3)
  Part3 = Arduino Uno (Rev3)
  J1 = Basic Servo
  hc-sr1 = hc-sr04
  LED1 = smd LED [color="Red (633nm)" package="1206 [SMD]"]
  LED2 = smd LED [color="Yellow (595nm)" package="1206 [SMD]"]
  LED3 = smd LED [color="Yellow (595nm)" package="1206 [SMD]"]
  LED4 = smd LED [color="Blue (525nm)" package="1206 [SMD]"]
  LED5 = smd LED [color="Blue (525nm)" package="1206 [SMD]"]

nets:
  N1: Part2.PWM_D9, J1.pulse
  GND: Part2.GND, Part3.GND, hc-sr1.GND
  N2: Part2.A4/SDA, Part3.A4/SDA
  N3: Part2.A5/SCL, Part3.A5/SCL
  N4: Part3.D8, LED5.anode
  N5: Part3.D9_PWM, LED4.anode
  N6: Part3.D10_PWM/SS, LED3.anode
  N7: Part3.D11_PWM/MOSI, LED2.anode
  N8: Part3.D12/MISO, LED1.anode
  N9: Part3.D4, hc-sr1.Trig
  N10: Part3.D5_PWM, hc-sr1.Echo
  5V: Part3.5V, hc-sr1.VCC
  N11: LED1.cathode, LED2.cathode, LED3.cathode, LED4.cathode, LED5.cathode

notes:
  [ External 7.4v power supply ]
